// Logisim project CPUdesign.circ as structural Verilog: 3 circuits, main circuit main
module main (
  input  rst
);

  wire alu_1_p4, clk_out, registerfile_1_p8, registerfile_1_p9, registerfile_1_p10;
  wire [4:0] rA, rB, rW;
  wire [31:0] adder_1_out, PC_q;

  Clock #(.highDuration(1), .lowDuration(1)) clk (.out(clk_out));
  Register #(.width(32), .trigger("rising"), .Select("low")) PC (
    .D(adder_1_out), .Q(PC_q), .clk(clk_out), .clr(rst));  // open: en
  Adder #(.width(32)) adder_1 (.a(32'h4), .b(PC_q), .out(adder_1_out));  // open: cin, cout
  // RegisterFile registerfile_1: pin names not known; wires that end beside it: rA, rB, rW, clk_out, rW, rA, rB, registerfile_1_p8, registerfile_1_p9, registerfile_1_p10, registerfile_1_p10
  // ALU alu_1: pin names not known; wires that end beside it: registerfile_1_p8, registerfile_1_p9, registerfile_1_p10, alu_1_p4
endmodule

module PC (
  input  [31:0] pcNew,
  input  clk,
  input  reset,
  output [31:0] pcOld
);

  Register #(.width(32), .trigger("rising"), .Select("low")) register_1 (
    .D(pcNew), .Q(pcOld), .clk(clk), .clr(reset));  // open: en
endmodule

module ALU (
  input  [31:0] A,
  input  [31:0] B,
  input  [15:0] imm,
  input  [4:0] Shamt,
  input  [1:0] ALUSrc,
  input  [3:0] op,
  output [31:0] ALUresult
);

  wire [31:0] adder_1_out, and_1_out, bit_extender_1_out, bit_extender_2_out, multiplexer_1_out,
       multiplier_1_out, or_1_out, shifter_1_out, shifter_2_out, shifter_3_out, xor_1_out;

  assign bit_extender_1_out = {{16{imm[15]}}, imm};  // Bit_Extender bit_extender_1
  assign bit_extender_2_out = {{16{1'b0}}, imm};  // Bit_Extender bit_extender_2
  Multiplexer #(.select(2), .width(32), .disabled("Z"), .enable("false")) multiplexer_1 (
    .in0(B), .in1(bit_extender_1_out), .in2(bit_extender_2_out), .in3({32{1'b0}}), .out(multiplexer_1_out),
    .sel(ALUSrc));
  assign and_1_out = A & multiplexer_1_out;  // AND_Gate and_1, 32 bits wide
  assign or_1_out = A | multiplexer_1_out;  // OR_Gate or_1, 32 bits wide
  assign xor_1_out = A ^ multiplexer_1_out;  // XOR_Gate xor_1, 32 bits wide
  Adder #(.width(32)) adder_1 (.a(A), .b(multiplexer_1_out), .out(adder_1_out));  // open: cin, cout
  Shifter #(.width(32), .shift("ll")) shifter_1 (.in(multiplexer_1_out), .\dist (Shamt), .out(shifter_1_out));
  Shifter #(.width(32), .shift("lr")) shifter_2 (.in(multiplexer_1_out), .\dist (Shamt), .out(shifter_2_out));
  Shifter #(.width(32), .shift("ll")) shifter_3 (.in(multiplexer_1_out), .\dist (5'b10000), .out(shifter_3_out));
  Multiplier #(.width(32)) multiplier_1 (.a(A), .b(multiplexer_1_out), .out(multiplier_1_out));  // open: cin, cout
  Multiplexer #(.select(4), .width(32), .disabled("Z"), .enable("false")) multiplexer_2 (
    .in0(and_1_out), .in1(or_1_out), .in2(xor_1_out), .in3(adder_1_out), .in4(shifter_1_out),
    .in5(shifter_2_out), .in6(shifter_3_out), .in7(multiplier_1_out), .out(ALUresult), .sel(op));  // open: in8, in9, in10, in11, in12, in13, in14, in15

  // Notes on the sheet:
  //   单元测试 
  //   lui
endmodule
